# Fritzing sketch bmp (saved by Fritzing 0.9.0b)
circuit board: 8.46667cm x 5.64444cm

parts:
  Part1 = Arduino Nano (Rev3.0)
  J1 = female pin header, 7 pins [form="♀ (female)"]
  J2 = female pin header, 7 pins [form="♀ (female)"]
  J3 = female pin header, 2 pins [form="♀ (female)"]
  J4 = female pin header, 2 pins [form="♀ (female)"]
  Q1 = MOSFET-NCHANNEL [package=to220v]
  R1 = Resistor [tolerance=±5% resistance=220 package=THT]

nets (from the schematic view):
  N1: Part1.RESET, J3.pin1, J4.pin1
  N2: Part1.GND, J1.pin3, J2.pin3
  N3: Part1.D9, J2.pin7
  N4: Part1.D10, J1.pin7
  N5: Part1.D11/MOSI, J1.pin6, J2.pin6
  N6: Part1.D12/MISO, J1.pin5, J2.pin5
  N7: Part1.VIN, J3.pin2, Q1.D
  N8: Part1.5V, J1.pin1, J2.pin1, R1.Pin_0
  N9: Part1.D13/SCK, J1.pin4, J2.pin4
  N10: J4.pin2, Q1.S
  N11: Q1.G, R1.Pin_1
