# Fritzing sketch sprinkler (saved by Fritzing 0.9.0b)
circuit board: 8.46667cm x 5.64444cm
breadboards: 1

parts:
  Part1 = Arduino Nano (Rev3.0)
  Part2 = Barometric Pressure Sensor - BMP085 Breakout
  Part3 = Humidity Temperature Sensor SHT15
  Part4 = Real Time Clock Module - DS1307 RTC Breakout Board

nets:
  GND: Part1.GND, Part2.GND, Part3.GND, Part4.GND
  5V: Part1.5V, Part2.VCC, Part3.VCC, Part4.5V
  N1: Part1.A5, Part2.SDA
  N2: Part1.A4, Part2.SCL
